// Logisim project LOgic circuit.circ as structural Verilog: 2 circuits, main circuit main
module main (
  input  in_1,
  input  in_2
);

  wire clock_1_out;
  wire [6:0] undriven;
  wire [31:0] adder_1_out, ram_1_data, register_1_q;

  Adder #(.width(32)) adder_1 (.a(register_1_q), .b(32'h4), .out(adder_1_out));  // open: cin, cout
  Clock clock_1 (.out(clock_1_out));
  Shifter #(.width(32), .shift("lr")) shifter_1 ();  // open: in, dist, out
  Register #(.width(32)) register_1 (.D(adder_1_out), .en(in_1), .Q(register_1_q), .clk(clock_1_out), .clr(in_2));
  RAM #(.addrWidth(24), .dataWidth(32)) ram_1 (
    .addr(register_1_q[25:2]), .data(ram_1_data), .sel(in_1), .clk(clock_1_out), .clr(in_2));  // open: ld
  Adder #(.width(7)) adder_2 (.a(undriven));  // open: b, out, cin, cout
endmodule

module Subtracter (
  input  in_1,
  input  in_2
);

  wire clock_1_out;
  wire [7:0] register_1_q, subtractor_1_out, undriven;

  Subtractor subtractor_1 (.a(register_1_q), .b(undriven), .out(subtractor_1_out));  // open: bin, bout
  Clock clock_1 (.out(clock_1_out));
  Register register_1 (.D(subtractor_1_out), .en(in_2), .Q(register_1_q), .clk(clock_1_out), .clr(in_1));
endmodule
